# Fritzing sketch diagram_harkka (saved by Fritzing 0.9.4)

parts:
  LCD1 = LCD screen
  Part1 = Arduino Mega 2560 (Rev3)
  Part2 = Arduino Uno (Rev3)
  R1 = Trimmer Potentiometer [maximum_resistance=10kΩ package=THT]
  Sensore_PIR_HC-SR502 = HC-SR501 Body Sensor Module
  R2 = Resistor [tolerance=±5% resistance=220 package=THT]
  LED1 = LED - 5mm [color="Red (633nm)" package="5 mm [THT]"]
  J1 = Piezo Speaker
  R3 = Resistor [tolerance=±5% resistance=220 package=THT]
  R4 = Resistor [tolerance=±5% resistance=100 package=THT]
  Keypad4x1 = Keypad Membran 4x4

nets:
  GND: LCD1.VSS, LCD1.LED-, Part1.GND, Part2.GND, R1.leg1, Sensore_PIR_HC-SR502.GND, LED1.cathode, J1.pin1
  VDD: LCD1.VDD, Part1.5V, R1.leg2, R2.Pin_1
  N1: LCD1.V0, R1.wiper
  N2: LCD1.RS, Part1.D9_PWM
  N3: LCD1.R/W, Part1.D10_PWM
  N4: LCD1.E, Part1.D11_PWM
  N5: LCD1.DB4, Part1.D3_PWM
  N6: LCD1.DB5, Part1.D4_PWM
  N7: LCD1.DB6, Part1.D5_PWM
  N8: LCD1.DB7, Part1.D7_PWM
  N9: LCD1.LED+, R2.Pin_0
  N10: Part1.A8, Keypad4x1.Pin1
  N11: Part1.A9, Keypad4x1.Pin2
  N12: Part1.A10, Keypad4x1.Pin3
  N13: Part1.A11, Keypad4x1.Pin4
  N14: Part1.A12, Keypad4x1.Pin5
  N15: Part1.A13, Keypad4x1.Pin6
  N16: Part1.A14, Keypad4x1.Pin7
  N17: Part1.A15, Keypad4x1.Pin8
  N18: Part1.D6_PWM, R4.Pin_0
  N19: Part1.D37, R3.Pin_0
  N20: Part1.D50, Part2.D12/MISO
  N21: Part1.D51, Part2.D11_PWM/MOSI
  N22: Part1.D52, Part2.D13/SCK
  N23: Part1.D53, Part2.D10_PWM/SS
  N24: Part2.D7, Sensore_PIR_HC-SR502.OUT
  5V: Part2.5V, Sensore_PIR_HC-SR502.VCC
  N25: LED1.anode, R3.Pin_1
  N26: J1.pin2, R4.Pin_1

custom parts:
  HC-SR501 Body Sensor Module: Pyroelectric Infrared PIR Motion Sensor Detector Module
  Keypad Membran 4x4: Membrane Keypad 4x4 Matrix
