# Fritzing sketch schematic_harkka (saved by Fritzing 0.9.4)
breadboards: 1

parts:
  MEGA = Arduino Mega 2560 (Rev3)
  UNO = Arduino Uno (Rev3) - ICSP
  LCD = LCD-16X2 [package=lcd-8x2-kit]
  SG1 = Buzzer 12mm [package=buzzer-ccv]
  LED1 = LED - 5mm [color="Red (633nm)" package="5 mm [THT]"]
  R1 = Resistor [tolerance=±5% resistance=220 package="1206 [SMD]"]
  R2 = Resistor [tolerance=±5% resistance=220 package="0402 [SMD]"]
  Keypad4x4 = Keypad Membran 4x4
  Motion_sensor = HC-SR501 Body Sensor Module
  R4 = Resistor [tolerance=±5% resistance=220 package="1206 [SMD]"]
  POT_10KΩ = TRIMPOT [package=trimpot-5mm]

nets:
  N1: MEGA.A8, Keypad4x4.Pin1
  N2: MEGA.A9, Keypad4x4.Pin2
  N3: MEGA.A10, Keypad4x4.Pin3
  N4: MEGA.A11, Keypad4x4.Pin4
  N5: MEGA.A12, Keypad4x4.Pin5
  N6: MEGA.A13, Keypad4x4.Pin6
  N7: MEGA.A14, Keypad4x4.Pin7
  N8: MEGA.A15, Keypad4x4.Pin8
  GND: MEGA.GND, UNO.GND, LCD.VSS, LCD.K, SG1.2, LED1.cathode, Motion_sensor.GND, POT_10KΩ.CW
  N9: MEGA.D11_PWM, LCD.E
  N10: MEGA.D10_PWM, LCD.R_W
  N11: MEGA.D9_PWM, LCD.RS
  5V: MEGA.5V, LCD.VDD, R4.Pin_0, POT_10KΩ.CCW
  N12: MEGA.D3_PWM, LCD.DB4
  N13: MEGA.D4_PWM, LCD.DB5
  N14: MEGA.D5_PWM, LCD.DB6
  N15: MEGA.D6_PWM, R2.Pin_0
  N16: MEGA.D7_PWM, LCD.DB7
  N17: MEGA.D37, R1.Pin_0
  N18: MEGA.D50, UNO.ICSP_MISO, UNO.D12/MISO
  N19: MEGA.D51, UNO.ICSP_MOSI, UNO.D11_PWM/MOSI
  N20: MEGA.D52, UNO.ICSP_SCK, UNO.D13/SCK
  N21: MEGA.D53, UNO.D10_PWM/SS
  5V_2: UNO.5V, Motion_sensor.VCC
  N22: UNO.D7, Motion_sensor.OUT
  N23: LCD.VO, POT_10KΩ.WIPER
  N24: LCD.A, R4.Pin_1
  N25: SG1.1, R2.Pin_1
  N26: LED1.anode, R1.Pin_1

custom parts:
  Keypad Membran 4x4: Membrane Keypad 4x4 Matrix
  HC-SR501 Body Sensor Module: Pyroelectric Infrared PIR Motion Sensor Detector Module
